# Fritzing sketch Binair knopje Schema (saved by Fritzing 0.9.10b)
breadboards: 2

parts:
  M1 = ESP32-S3-DevKitC-1 [part_number=ESP32-S3-DevKitC-1]
  D1 = LED_BARGRAPH_10 [package=led_bargaph_10]
  R1 = Resistor [tolerance=±5% resistance=220 package="0805 [SMD]"]
  R2 = Resistor [tolerance=±5% resistance=220 package="0805 [SMD]"]
  R3 = Resistor [tolerance=±5% resistance=220 package="0805 [SMD]"]
  R4 = Resistor [tolerance=±5% resistance=220 package="0805 [SMD]"]
  R5 = Resistor [tolerance=±5% resistance=220 package="0805 [SMD]"]
  R6 = Resistor [tolerance=±5% resistance=220 package="0805 [SMD]"]
  R7 = Resistor [tolerance=±5% resistance=220 package="0805 [SMD]"]
  R8 = Resistor [tolerance=±5% resistance=220 package="0805 [SMD]"]
  R9 = Resistor [tolerance=±5% resistance=220 package="0805 [SMD]"]
  R10 = Resistor [tolerance=±5% resistance=220 package="0805 [SMD]"]
  S1 = Momentary Switch [package=ksa_sealed_tac_switch]
  S2 = Momentary Switch [package=ksa_sealed_tac_switch]
  R11 = Resistor [tolerance=±5% resistance=220 package="2010 [SMD]"]
  R12 = Resistor [tolerance=±5% resistance=220 package="2010 [SMD]"]

nets:
  N1: M1.pin_1, M1.pin_2, S1.1, S2.1
  N2: M1.pin_4, R1.Pin_1
  N3: M1.pin_5, R2.Pin_1
  N4: M1.pin_6, R3.Pin_1
  N5: M1.pin_7, R4.Pin_1
  N6: M1.pin_8, R5.Pin_1
  N7: M1.pin_9, R6.Pin_1
  N8: M1.pin_13, R7.Pin_1
  N9: M1.pin_14, R8.Pin_1
  N10: M1.pin_15, R9.Pin_1
  N11: M1.pin_16, R10.Pin_1
  N12: D1.A_A, D1.B_A, D1.C_A, D1.D_A, D1.E_A, D1.F_A, D1.G_A, D1.H_A, D1.I_A, D1.J_A, R11.Pin_1, R12.Pin_1
  N13: D1.J_C, R10.Pin_0
  N14: D1.I_C, R9.Pin_0
  N15: D1.H_C, R8.Pin_0
  N16: D1.G_C, R7.Pin_0
  N17: D1.F_C, R6.Pin_0
  N18: D1.E_C, R5.Pin_0
  N19: D1.D_C, R4.Pin_0
  N20: D1.C_C, R3.Pin_0
  N21: D1.B_C, R2.Pin_0
  N22: D1.A_C, R1.Pin_0
  N23: S1.2, R11.Pin_0
  N24: S2.2, R12.Pin_0

custom parts:
  ESP32-S3-DevKitC-1: ESP32-S2-DevKitC-1 is an entry-level development board based on ESP32-S2-SOLO (on-board PCB antenna). It is based on the ESP32 microcontroller that boasts Wifi, Bluetooth, Ethernet and Low Power support all in a single chip. (vanepp) Feb 2022: converted to ESP32-S2-DevKitC-1. This module is 44pins long (2x22) and 11 pins width.
