# Fritzing sketch Lightrider Schema (saved by Fritzing 0.9.10b)
breadboards: 2

parts:
  M1 = ESP32-S3-DevKitC-1 [part_number=ESP32-S3-DevKitC-1]
  D1 = LED_BARGRAPH_10 [package=led_bargaph_10]
  R1 = Resistor [tolerance=±5% power=0.25 resistance=220 package=THT]
  R2 = Resistor [tolerance=±5% power=0.25 resistance=220 package=THT]
  R3 = Resistor [tolerance=±5% power=0.25 resistance=220 package=THT]
  R4 = Resistor [tolerance=±5% power=0.25 resistance=220 package=THT]
  R5 = Resistor [tolerance=±5% power=0.25 resistance=220 package=THT]
  R6 = Resistor [tolerance=±5% power=0.25 resistance=220 package=THT]
  R7 = Resistor [tolerance=±5% power=0.25 resistance=220 package=THT]
  R8 = Resistor [tolerance=±5% power=0.25 resistance=220 package=THT]
  R9 = Resistor [tolerance=±5% power=0.25 resistance=220 package=THT]
  R11 = Resistor [tolerance=±5% power=0.25 resistance=220 package=THT]
  R13 = Rotary Potentiometer (Large) [maximum_resistance=100kΩ knob_status=50% power=0.5W package=THT]

nets:
  N1: M1.pin_1, M1.pin_2, R13.leg1
  N2: M1.pin_4, D1.J_A
  N3: M1.pin_5, D1.I_A
  N4: M1.pin_6, D1.H_A
  N5: M1.pin_7, D1.G_A
  N6: M1.pin_8, D1.F_A
  N7: M1.pin_9, D1.E_A
  N8: M1.pin_10, D1.D_A
  N9: M1.pin_11, D1.C_A
  N10: M1.pin_12, D1.B_A
  N11: M1.pin_13, D1.A_A
  N12: M1.pin_22, M1.pin_23, M1.pin_24, M1.pin_44, R1.Pin_0, R2.Pin_0, R3.Pin_0, R4.Pin_0, R5.Pin_0, R6.Pin_0, R7.Pin_0, R8.Pin_0, R9.Pin_0, R11.Pin_0, R13.leg2
  N13: M1.pin_40, R13.wiper
  N14: D1.J_C, R5.Pin_1
  N15: D1.I_C, R6.Pin_1
  N16: D1.H_C, R7.Pin_1
  N17: D1.G_C, R8.Pin_1
  N18: D1.F_C, R9.Pin_1
  N19: D1.E_C, R11.Pin_1
  N20: D1.D_C, R4.Pin_1
  N21: D1.C_C, R3.Pin_1
  N22: D1.B_C, R2.Pin_1
  N23: D1.A_C, R1.Pin_1

custom parts:
  ESP32-S3-DevKitC-1: ESP32-S2-DevKitC-1 is an entry-level development board based on ESP32-S2-SOLO (on-board PCB antenna). It is based on the ESP32 microcontroller that boasts Wifi, Bluetooth, Ethernet and Low Power support all in a single chip. (vanepp) Feb 2022: converted to ESP32-S2-DevKitC-1. This module is 44pins long (2x22) and 11 pins width.
