# Fritzing sketch Stoplicht (saved by Fritzing 0.9.10b)
breadboards: 2

parts:
  M1 = ESP32-S3-DevKitC-1 [part_number=ESP32-S3-DevKitC-1]
  LED1 = smd LED [color="Yellow (595nm)" package="0603 [SMD]"]
  LED3 = smd LED [color="Red (660nm)" package="0603 [SMD]"]
  LED2 = smd LED [color="Green (570nm)" part_number=BBAA100043 package="0805 [SMD]"]
  S1 = Momentary Switch [package=ksa_sealed_tac_switch]
  R1 = Resistor [tolerance=±5% resistance=220 package="0805 [SMD]"]
  R2 = Resistor [tolerance=±5% resistance=220 package="0805 [SMD]"]
  R3 = Resistor [tolerance=±5% resistance=220 package="0805 [SMD]"]
  R4 = Resistor [tolerance=±5% resistance=220 package="0805 [SMD]"]

nets:
  N1: M1.pin_1, M1.pin_2, S1.1
  N2: M1.pin_22, M1.pin_23, M1.pin_24, M1.pin_44, R1.Pin_1, R2.Pin_1, R3.Pin_1, R4.Pin_1
  N3: M1.pin_33, LED3.cathode, R1.Pin_0
  N4: M1.pin_34, LED1.cathode, R2.Pin_0
  N5: M1.pin_35, LED2.anode
  N6: M1.pin_37, S1.3
  N7: LED2.cathode, R3.Pin_0
  N8: S1.4, R4.Pin_0

custom parts:
  ESP32-S3-DevKitC-1: ESP32-S2-DevKitC-1 is an entry-level development board based on ESP32-S2-SOLO (on-board PCB antenna). It is based on the ESP32 microcontroller that boasts Wifi, Bluetooth, Ethernet and Low Power support all in a single chip. (vanepp) Feb 2022: converted to ESP32-S2-DevKitC-1. This module is 44pins long (2x22) and 11 pins width.
