# Fritzing sketch Template ESP (saved by Fritzing 0.9.10b)
breadboards: 2

parts:
  M1 = ESP32-S3-DevKitC-1 [part_number=ESP32-S3-DevKitC-1]

nets:
  N1: M1.pin_1, M1.pin_2
  N2: M1.pin_22, M1.pin_23, M1.pin_24, M1.pin_44

custom parts:
  ESP32-S3-DevKitC-1: ESP32-S2-DevKitC-1 is an entry-level development board based on ESP32-S2-SOLO (on-board PCB antenna). It is based on the ESP32 microcontroller that boasts Wifi, Bluetooth, Ethernet and Low Power support all in a single chip. (vanepp) Feb 2022: converted to ESP32-S2-DevKitC-1. This module is 44pins long (2x22) and 11 pins width.
